# Fritzing sketch RTC_LCD_ARDUINO (saved by Fritzing 0.9.3b)

parts:
  元件1 = LCD Display 16x2
  LCM1602_IIC1 = LCM1602 IIC [part_number="LCM1602 IIC" chip_label="LCM1602 IIC" package="DIP (Dual Inline) [THT]"]
  PCB2 = RTC_DS1302_module
  Componente1 = Arduino Uno (Rev3)
  U1 = SWITCH_SPDT [package=kps-1290]

nets:
  N1: 元件1.aún_sin_nombre#0, LCM1602_IIC1.VSS
  N2: 元件1.aún_sin_nombre#1, LCM1602_IIC1.VDD
  N3: 元件1.aún_sin_nombre#2, LCM1602_IIC1.V0
  N4: 元件1.aún_sin_nombre#3, LCM1602_IIC1.RS
  N5: 元件1.aún_sin_nombre#4, LCM1602_IIC1.RW
  N6: 元件1.aún_sin_nombre#5, LCM1602_IIC1.E
  N7: 元件1.aún_sin_nombre#6, LCM1602_IIC1.D0
  N8: 元件1.aún_sin_nombre#7, LCM1602_IIC1.D1
  N9: 元件1.aún_sin_nombre#8, LCM1602_IIC1.D2
  N10: 元件1.aún_sin_nombre#9, LCM1602_IIC1.D3
  N11: 元件1.aún_sin_nombre#10, LCM1602_IIC1.D4
  N12: 元件1.aún_sin_nombre#11, LCM1602_IIC1.D5
  N13: 元件1.aún_sin_nombre#12, LCM1602_IIC1.D6
  N14: 元件1.aún_sin_nombre#13, LCM1602_IIC1.D7
  N15: 元件1.aún_sin_nombre#14, LCM1602_IIC1.A
  N16: 元件1.aún_sin_nombre#15, LCM1602_IIC1.K
  GND: LCM1602_IIC1.GND, PCB2.GND, Componente1.GND, U1.O
  N17: LCM1602_IIC1.SDA, Componente1.A4/SDA
  N18: LCM1602_IIC1.SCL, Componente1.A5/SCL
  VCC: PCB2.VCC, Componente1.5V
  N19: PCB2.RST, Componente1.D2
  N20: PCB2.DAT, Componente1.D3_PWM
  N21: PCB2.CLK, Componente1.D4
  N22: Componente1.D7, U1.P

custom parts:
  LCM1602 IIC: I2C-Module to use a 1602 or 2004 LCD on with the wire.h libory Serial LCD Modul
  RTC_DS1302_module: Arduino module DS1302 SPI Real Time Clock
