# Fritzing sketch SimpleSecuritySystem (saved by Fritzing 0.9.3b)
breadboards: 1

parts:
  元件1 = Arduino Mega 2560 (Rev3)
  S1 = Reed switch [package=THT]
  R1 = Resistor [tolerance=±5% resistance=10k package=THT]
  SW1 = DIP SWITCH [package=dipswitch-02]
  R2 = Resistor [tolerance=±5% resistance=10k package=THT]
  J1 = Piezo Speaker
  Grove1 = Grove OLED 128x96

nets:
  N1: 元件1.D21/SCL, Grove1.SCL
  N2: 元件1.D20/SDA, Grove1.SDA
  GND: 元件1.GND, S1.pin_2, R2.Pin_1, J1.pin1, Grove1.GND
  5V: 元件1.5V, R1.Pin_0, SW1.4, Grove1.VCC
  N3: 元件1.D2_PWM, S1.pin_1, R1.Pin_1
  N4: 元件1.D3_PWM, SW1.1, R2.Pin_0
  N5: 元件1.D4_PWM, J1.pin2
